// Logisim project Aula1.circ as structural Verilog: 4 circuits, main circuit main
module main (
  input  [3:0] A,
  input  [3:0] B,
  input  [3:0] C,
  input  [3:0] D,
  input  [1:0] CH,
  output [3:0] S
);

  Multiplexer #(.select(2), .width(4), .enable("false")) multiplexer_1 (
    .in0(A), .in1(B), .in2(C), .in3(D), .out(S), .sel(CH));
endmodule

module meioSomador (
  input  A,
  input  B,
  output S,
  output Cout
);

  xor xor_1 (S, A, B);
  and and_1 (Cout, A, B);
endmodule

module somadorCompleto (
  input  A,
  input  B,
  input  Cin,
  output S,
  output Cout
);

  wire meiosomador_1_cout, meiosomador_1_s, meiosomador_2_cout;

  meioSomador meiosomador_1 (.Cout(meiosomador_1_cout), .S(meiosomador_1_s), .B(B), .A(A));
  meioSomador meiosomador_2 (.Cout(meiosomador_2_cout), .S(S), .B(Cin), .A(meiosomador_1_s));
  or or_1 (Cout, meiosomador_2_cout, meiosomador_1_cout);
endmodule

module somador_4bits (
  input  [3:0] A,
  input  [3:0] B,
  output [3:0] S
);

  wire somadorcompleto_1_cout, somadorcompleto_2_cout, somadorcompleto_3_cout, somadorcompleto_4_cout;

  somadorCompleto somadorcompleto_1 (
    .Cout(somadorcompleto_1_cout), .S(S[3]), .Cin(somadorcompleto_2_cout), .B(B[3]), .A(A[3]));
  somadorCompleto somadorcompleto_2 (
    .Cout(somadorcompleto_2_cout), .S(S[2]), .Cin(somadorcompleto_3_cout), .B(B[2]), .A(A[2]));
  Hex_Digit_Display hex_digit_display_1 (.value(S));  // open: dp
  somadorCompleto somadorcompleto_3 (
    .Cout(somadorcompleto_3_cout), .S(S[1]), .Cin(somadorcompleto_4_cout), .B(B[1]), .A(A[1]));
  somadorCompleto somadorcompleto_4 (.Cout(somadorcompleto_4_cout), .S(S[0]), .Cin(1'b0), .B(B[0]), .A(A[0]));
  // also tied to GND on the sheet: somadorcompleto_1_cout
endmodule
