// Logisim project ProjetoULA_Eduardo_Karpfenstein_77.circ as structural Verilog: 8 circuits, main circuit main
module main (
  input  [2:0] in_1,
  input  [2:0] in_2,
  input  [7:0] in_3,
  input  [3:0] in_4,
  input  [7:0] in_5,
  input  in_6,
  input  [3:0] in_7,
  input  [2:0] in_8,
  input  [2:0] in_9,
  output [7:0] out_10
);

  ULA ula_1 (
    .in_8(in_9), .CH_AB(in_6), .in_6(in_8), .B(in_5), .CH_A(in_4), .A(in_3), .in_2(in_2), .in_1(in_1),
    .CH_B(in_7), .S(out_10));
endmodule

module ULA (
  input  [2:0] in_1,
  input  [2:0] in_2,
  input  [7:0] A,
  input  [3:0] CH_A,
  input  [7:0] B,
  input  [2:0] in_6,
  input  CH_AB,
  input  [2:0] in_8,
  input  [3:0] CH_B,
  output [7:0] S
);

  wire [7:0] and_1_out, demultiplexer_1_out0, demultiplexer_1_out1, demultiplexer_1_out2,
       demultiplexer_1_out4, demultiplexer_1_out5, demultiplexer_1_out7, demultiplexer_1_out8,
       demultiplexer_1_out9, demultiplexer_1_out10, demultiplexer_1_out11, demultiplexer_1_out12,
       demultiplexer_1_out14, demultiplexer_1_out15, demultiplexer_2_out0, demultiplexer_2_out1,
       demultiplexer_2_out2, demultiplexer_2_out4, demultiplexer_2_out5, demultiplexer_2_out7,
       demultiplexer_2_out8, demultiplexer_2_out9, demultiplexer_2_out10, demultiplexer_2_out11,
       demultiplexer_2_out12, demultiplexer_2_out14, demultiplexer_2_out15, multiplexer_1_out,
       multiplexer_2_out, multiplier_1_out, nand_1_out, nor_1_out, not_1_out, not_2_out, or_1_out,
       shifter_1_out, shifter_2_out, shifter_3_out, shifter_4_out, somador8bits_1_s, subtrator8bits_1_out_5,
       xnor_1_out, xor_1_out;

  Demultiplexer #(.select(4), .width(8), .enable("false")) demultiplexer_1 (
    .out0(demultiplexer_1_out0), .out1(demultiplexer_1_out1), .out2(demultiplexer_1_out2),
    .out3(demultiplexer_1_out0), .out4(demultiplexer_1_out4), .out5(demultiplexer_1_out5),
    .out6(demultiplexer_1_out0), .out7(demultiplexer_1_out7), .out8(demultiplexer_1_out8),
    .out9(demultiplexer_1_out9), .out10(demultiplexer_1_out10), .out11(demultiplexer_1_out11),
    .out12(demultiplexer_1_out12), .out13(demultiplexer_1_out0), .out14(demultiplexer_1_out14),
    .out15(demultiplexer_1_out15), .in(A), .sel(CH_A));
  Demultiplexer #(.select(4), .width(8), .enable("false")) demultiplexer_2 (
    .out0(demultiplexer_2_out0), .out1(demultiplexer_2_out1), .out2(demultiplexer_2_out2),
    .out3(demultiplexer_2_out0), .out4(demultiplexer_2_out4), .out5(demultiplexer_2_out5),
    .out6(demultiplexer_2_out0), .out7(demultiplexer_2_out7), .out8(demultiplexer_2_out8),
    .out9(demultiplexer_2_out9), .out10(demultiplexer_2_out10), .out11(demultiplexer_2_out11),
    .out12(demultiplexer_2_out12), .out13(demultiplexer_2_out0), .out14(demultiplexer_2_out14),
    .out15(demultiplexer_2_out15), .in(B), .sel(CH_B));
  Multiplier multiplier_1 (
    .a(demultiplexer_1_out8), .b(demultiplexer_2_out8), .out(multiplier_1_out), .cin(demultiplexer_1_out0),
    .cout(demultiplexer_2_out0));
  assign nor_1_out = ~(demultiplexer_1_out1 | demultiplexer_2_out1);  // NOR_Gate nor_1, 8 bits wide
  Subtrator8bits subtrator8bits_1 (
    .out_5(subtrator8bits_1_out_5), .B(demultiplexer_2_out15), .Bin(1'b0), .A(demultiplexer_1_out15),
    .Bout(1'b0));
  Somador8bits somador8bits_1 (
    .S(somador8bits_1_s), .B(demultiplexer_2_out12), .A(demultiplexer_1_out12), .in_4(1'b0), .in_3(1'b0));
  Shifter #(.shift("lr")) shifter_1 (.in(demultiplexer_1_out5), .\dist (in_1), .out(shifter_1_out));
  Shifter shifter_2 (.in(demultiplexer_1_out10), .\dist (in_2), .out(shifter_2_out));
  assign and_1_out = demultiplexer_1_out9 & demultiplexer_2_out9;  // AND_Gate and_1, 8 bits wide
  assign or_1_out = demultiplexer_1_out14 | demultiplexer_2_out14;  // OR_Gate or_1, 8 bits wide
  assign nand_1_out = ~(demultiplexer_1_out4 & demultiplexer_2_out4);  // NAND_Gate nand_1, 8 bits wide
  assign xor_1_out = demultiplexer_1_out7 ^ demultiplexer_2_out7;  // XOR_Gate xor_1, 8 bits wide
  assign xnor_1_out = ~(demultiplexer_1_out11 ^ demultiplexer_2_out11);  // XNOR_Gate xnor_1, 8 bits wide
  Shifter #(.shift("lr")) shifter_3 (.in(demultiplexer_2_out5), .\dist (in_6), .out(shifter_3_out));
  Shifter shifter_4 (.in(demultiplexer_2_out10), .\dist (in_8), .out(shifter_4_out));
  assign not_1_out = ~demultiplexer_1_out2;  // NOT_Gate not_1, 8 bits wide
  assign not_2_out = ~demultiplexer_2_out2;  // NOT_Gate not_2, 8 bits wide
  Multiplexer #(.select(4), .width(8), .enable("false")) multiplexer_1 (
    .in0({8{1'b0}}), .in1(nor_1_out), .in2(not_1_out), .in3({8{1'b0}}), .in4(nand_1_out),
    .in5(shifter_1_out), .in6({8{1'b0}}), .in7(xor_1_out), .in8(multiplier_1_out), .in9(and_1_out),
    .in10(shifter_2_out), .in11(xnor_1_out), .in12(somador8bits_1_s), .in13({8{1'b0}}), .in14(or_1_out),
    .in15(subtrator8bits_1_out_5), .out(multiplexer_1_out), .sel(CH_A));
  Multiplexer #(.select(4), .width(8), .enable("false")) multiplexer_2 (
    .in0({8{1'b0}}), .in1(nor_1_out), .in2(not_2_out), .in3({8{1'b0}}), .in4(nand_1_out),
    .in5(shifter_3_out), .in7(xor_1_out), .in8(multiplier_1_out), .in9(and_1_out), .in10(shifter_4_out),
    .in11(xnor_1_out), .in12(somador8bits_1_s), .in13({8{1'b0}}), .in14(or_1_out),
    .in15(subtrator8bits_1_out_5), .out(multiplexer_2_out), .sel(CH_B));  // open: in6
  Multiplexer #(.width(8), .enable("false")) multiplexer_3 (
    .in0(multiplexer_1_out), .in1(multiplexer_2_out), .out(S), .sel(CH_AB));
  // also tied to GND on the sheet: {demultiplexer_1_out0[0], demultiplexer_1_out0[1], demultiplexer_1_out0[2], demultiplexer_1_out0[3], demultiplexer_1_out0[4], demultiplexer_1_out0[5], demultiplexer_1_out0[6], demultiplexer_1_out0[7], demultiplexer_2_out0[0], demultiplexer_2_out0[1], demultiplexer_2_out0[2], demultiplexer_2_out0[3], demultiplexer_2_out0[4], demultiplexer_2_out0[5], demultiplexer_2_out0[6], demultiplexer_2_out0[7]}
endmodule

module MeioSomador (
  input  A,
  input  B,
  output out_3,
  output out_4
);

  xor xor_1 (out_3, A, B);
  and and_1 (out_4, A, B);
endmodule

module SomadorCompleto (
  input  A,
  input  B,
  input  Cin,
  output S,
  output Cout
);

  wire meiosomador_1_out_3, meiosomador_1_out_4, meiosomador_2_out_4;

  MeioSomador meiosomador_1 (.out_3(meiosomador_1_out_3), .B(B), .A(A), .out_4(meiosomador_1_out_4));
  MeioSomador meiosomador_2 (.out_3(S), .B(Cin), .A(meiosomador_1_out_3), .out_4(meiosomador_2_out_4));
  or or_1 (Cout, meiosomador_2_out_4, meiosomador_1_out_4);
endmodule

module MeioSubtrator (
  input  A,
  input  B,
  output out_3,
  output out_4
);

  xor xor_1 (out_3, A, B);
  and and_1 (out_4, B, ~A);  // AND_Gate
endmodule

module SubtratorCompleto (
  input  in_1,
  input  in_2,
  input  in_3,
  output out_4,
  output out_5
);

  wire meiosubtrator_1_out_3, meiosubtrator_1_out_4, meiosubtrator_2_out_4;

  MeioSubtrator meiosubtrator_1 (.out_4(meiosubtrator_1_out_4), .out_3(meiosubtrator_1_out_3), .B(in_2), .A(in_1));
  MeioSubtrator meiosubtrator_2 (.out_4(meiosubtrator_2_out_4), .out_3(out_4), .B(in_3), .A(meiosubtrator_1_out_3));
  or or_1 (out_5, meiosubtrator_2_out_4, meiosubtrator_1_out_4);
endmodule

module Somador8bits (
  input  [7:0] A,
  input  [7:0] B,
  input  in_3,
  input  in_4,
  output [7:0] S
);

  wire somadorcompleto_2_cout, somadorcompleto_3_cout, somadorcompleto_4_cout, somadorcompleto_5_cout,
       somadorcompleto_6_cout, somadorcompleto_7_cout, somadorcompleto_8_cout;

  SomadorCompleto somadorcompleto_1 (.Cout(in_4), .S(S[7]), .Cin(somadorcompleto_2_cout), .B(B[7]), .A(A[7]));
  SomadorCompleto somadorcompleto_2 (
    .Cout(somadorcompleto_2_cout), .S(S[6]), .Cin(somadorcompleto_3_cout), .B(B[6]), .A(A[6]));
  SomadorCompleto somadorcompleto_3 (
    .Cout(somadorcompleto_3_cout), .S(S[5]), .Cin(somadorcompleto_4_cout), .B(B[5]), .A(A[5]));
  SomadorCompleto somadorcompleto_4 (
    .Cout(somadorcompleto_4_cout), .S(S[4]), .Cin(somadorcompleto_5_cout), .B(B[4]), .A(A[4]));
  SomadorCompleto somadorcompleto_5 (
    .Cout(somadorcompleto_5_cout), .S(S[3]), .Cin(somadorcompleto_6_cout), .B(B[3]), .A(A[3]));
  SomadorCompleto somadorcompleto_6 (
    .Cout(somadorcompleto_6_cout), .S(S[2]), .Cin(somadorcompleto_7_cout), .B(B[2]), .A(A[2]));
  SomadorCompleto somadorcompleto_7 (
    .Cout(somadorcompleto_7_cout), .S(S[1]), .Cin(somadorcompleto_8_cout), .B(B[1]), .A(A[1]));
  SomadorCompleto somadorcompleto_8 (.Cout(somadorcompleto_8_cout), .S(S[0]), .Cin(in_3), .B(B[0]), .A(A[0]));
endmodule

module Subtrator8bits (
  input  [7:0] A,
  input  [7:0] B,
  input  Bin,
  input  Bout,
  output [7:0] out_5
);

  wire subtratorcompleto_2_out_5, subtratorcompleto_3_out_5, subtratorcompleto_4_out_5,
       subtratorcompleto_5_out_5, subtratorcompleto_6_out_5, subtratorcompleto_7_out_5,
       subtratorcompleto_8_out_5;

  SubtratorCompleto subtratorcompleto_1 (
    .out_5(Bout), .out_4(out_5[7]), .in_3(subtratorcompleto_2_out_5), .in_2(B[7]), .in_1(A[7]));
  SubtratorCompleto subtratorcompleto_2 (
    .out_5(subtratorcompleto_2_out_5), .out_4(out_5[6]), .in_3(subtratorcompleto_3_out_5), .in_2(B[6]),
    .in_1(A[6]));
  SubtratorCompleto subtratorcompleto_3 (
    .out_5(subtratorcompleto_3_out_5), .out_4(out_5[5]), .in_3(subtratorcompleto_4_out_5), .in_2(B[5]),
    .in_1(A[5]));
  SubtratorCompleto subtratorcompleto_4 (
    .out_5(subtratorcompleto_4_out_5), .out_4(out_5[4]), .in_3(subtratorcompleto_5_out_5), .in_2(B[4]),
    .in_1(A[4]));
  SubtratorCompleto subtratorcompleto_5 (
    .out_5(subtratorcompleto_5_out_5), .out_4(out_5[3]), .in_3(subtratorcompleto_6_out_5), .in_2(B[3]),
    .in_1(A[3]));
  SubtratorCompleto subtratorcompleto_6 (
    .out_5(subtratorcompleto_6_out_5), .out_4(out_5[2]), .in_3(subtratorcompleto_7_out_5), .in_2(B[2]),
    .in_1(A[2]));
  SubtratorCompleto subtratorcompleto_7 (
    .out_5(subtratorcompleto_7_out_5), .out_4(out_5[1]), .in_3(subtratorcompleto_8_out_5), .in_2(B[1]),
    .in_1(A[1]));
  SubtratorCompleto subtratorcompleto_8 (
    .out_5(subtratorcompleto_8_out_5), .out_4(out_5[0]), .in_3(Bin), .in_2(B[0]), .in_1(A[0]));
endmodule
