// Logisim project Relatorio1.circ as structural Verilog: 6 circuits, main circuit main
module main (
  input  [1:0] in_1,
  input  CH,
  input  in_3,
  input  [1:0] in_4,
  input  in_5,
  input  in_6,
  output [1:0] out_7,
  output [1:0] out_8
);

  wire undriven, undriven_2;
  wire [1:0] demultiplexer_1_out0, demultiplexer_1_out1, demultiplexer_2_out0, demultiplexer_2_out1,
       meiosomador_1_s, meiosubtrator_1_s, somadorcompleto_1_s, subtratorcomopleto_1_s;

  Demultiplexer #(.width(2), .enable("false")) demultiplexer_1 (
    .out0(demultiplexer_1_out0), .out1(demultiplexer_1_out1), .in(in_1), .sel(CH));
  Demultiplexer #(.width(2), .enable("false")) demultiplexer_2 (
    .out0(demultiplexer_2_out0), .out1(demultiplexer_2_out1), .in(in_4), .sel(in_5));
  meioSomador meiosomador_1 (
    .Cout(meiosomador_1_s[1]), .B(demultiplexer_1_out0[1]), .A(demultiplexer_1_out0[0]),
    .S(meiosomador_1_s[0]));
  meioSubtrator meiosubtrator_1 (
    .Tout(meiosubtrator_1_s[1]), .S(meiosubtrator_1_s[0]), .B(demultiplexer_1_out1[1]),
    .A(demultiplexer_1_out1[0]));
  somadorCompleto somadorcompleto_1 (
    .S(somadorcompleto_1_s[0]), .B(demultiplexer_2_out0[1]), .Cin(undriven), .Cout(somadorcompleto_1_s[1]),
    .A(demultiplexer_2_out0[0]));
  subtratorComopleto subtratorcomopleto_1 (
    .Bout(subtratorcomopleto_1_s[1]), .S(subtratorcomopleto_1_s[0]), .Bin(undriven_2),
    .B(demultiplexer_2_out1[1]), .A(demultiplexer_2_out1[0]));
  Multiplexer #(.width(2), .enable("false")) multiplexer_1 (
    .in0(meiosomador_1_s), .in1(meiosubtrator_1_s), .out(out_7), .sel(in_3));
  Multiplexer #(.width(2), .enable("false")) multiplexer_2 (
    .in0(somadorcompleto_1_s), .in1(subtratorcomopleto_1_s), .out(out_8), .sel(in_6));

  // Notes on the sheet:
  //   Meio Somador
  //   Meio Subtrator
  //   Somador Completo
  //   Subtrator Completo
endmodule

module meioSomador (
  input  A,
  input  B,
  output S,
  output Cout
);

  xor xor_1 (S, A, B);
  and and_1 (Cout, A, B);
endmodule

module somadorCompleto (
  input  A,
  input  B,
  input  Cin,
  output S,
  output Cout
);

  wire meiosomador_1_cout, meiosomador_1_s, meiosomador_2_cout;

  meioSomador meiosomador_1 (.Cout(meiosomador_1_cout), .B(B), .A(A), .S(meiosomador_1_s));
  meioSomador meiosomador_2 (.Cout(meiosomador_2_cout), .B(Cin), .A(meiosomador_1_s), .S(S));
  or or_1 (Cout, meiosomador_2_cout, meiosomador_1_cout);
endmodule

module somador_4bits (
  input  [3:0] A,
  input  [3:0] B,
  output [3:0] S
);

  wire somadorcompleto_1_cout, somadorcompleto_2_cout, somadorcompleto_3_cout, somadorcompleto_4_cout;

  somadorCompleto somadorcompleto_1 (
    .S(S[3]), .B(B[3]), .Cin(somadorcompleto_2_cout), .Cout(somadorcompleto_1_cout), .A(A[3]));
  somadorCompleto somadorcompleto_2 (
    .S(S[2]), .B(B[2]), .Cin(somadorcompleto_3_cout), .Cout(somadorcompleto_2_cout), .A(A[2]));
  Hex_Digit_Display hex_digit_display_1 (.value(S));  // open: dp
  somadorCompleto somadorcompleto_3 (
    .S(S[1]), .B(B[1]), .Cin(somadorcompleto_4_cout), .Cout(somadorcompleto_3_cout), .A(A[1]));
  somadorCompleto somadorcompleto_4 (.S(S[0]), .B(B[0]), .Cin(1'b0), .Cout(somadorcompleto_4_cout), .A(A[0]));
  // also tied to GND on the sheet: somadorcompleto_1_cout
endmodule

module meioSubtrator (
  input  A,
  input  B,
  output S,
  output Tout
);

  wire not_1_out;

  xor xor_1 (S, A, B);
  and and_1 (Tout, A, not_1_out);
  not not_1 (not_1_out, B);
endmodule

module subtratorComopleto (
  input  A,
  input  B,
  input  Bin,
  output S,
  output Bout
);

  wire meiosubtrator_1_s, meiosubtrator_1_tout, meiosubtrator_2_tout;

  meioSubtrator meiosubtrator_1 (.Tout(meiosubtrator_1_tout), .S(meiosubtrator_1_s), .B(B), .A(A));
  meioSubtrator meiosubtrator_2 (.Tout(meiosubtrator_2_tout), .S(S), .B(Bin), .A(meiosubtrator_1_s));
  or or_1 (Bout, meiosubtrator_2_tout, meiosubtrator_1_tout);
endmodule
