// Logisim project Relatorio2.circ as structural Verilog: 9 circuits, main circuit main
module main (
  input  [1:0] in_1,
  input  CH,
  input  in_3,
  input  [1:0] in_4,
  input  in_5,
  input  in_6,
  output [1:0] out_7,
  output [1:0] out_8
);

  wire undriven, undriven_2;
  wire [1:0] demultiplexer_1_out0, demultiplexer_1_out1, demultiplexer_2_out0, demultiplexer_2_out1,
       meiosomador_1_s, meiosubtrator_1_s, somadorcompleto_1_s, subtratorcomopleto_1_s;

  Demultiplexer #(.width(2), .enable("false")) demultiplexer_1 (
    .out0(demultiplexer_1_out0), .out1(demultiplexer_1_out1), .in(in_1), .sel(CH));
  Demultiplexer #(.width(2), .enable("false")) demultiplexer_2 (
    .out0(demultiplexer_2_out0), .out1(demultiplexer_2_out1), .in(in_4), .sel(in_5));
  meioSomador meiosomador_1 (
    .Cout(meiosomador_1_s[1]), .S(meiosomador_1_s[0]), .A(demultiplexer_1_out0[0]),
    .B(demultiplexer_1_out0[1]));
  meioSubtrator meiosubtrator_1 (
    .S(meiosubtrator_1_s[0]), .Tout(meiosubtrator_1_s[1]), .B(demultiplexer_1_out1[1]),
    .A(demultiplexer_1_out1[0]));
  somadorCompleto somadorcompleto_1 (
    .B(demultiplexer_2_out0[1]), .Cout(somadorcompleto_1_s[1]), .Cin(undriven), .S(somadorcompleto_1_s[0]),
    .A(demultiplexer_2_out0[0]));
  subtratorComopleto subtratorcomopleto_1 (
    .Bout(subtratorcomopleto_1_s[1]), .Bin(undriven_2), .S(subtratorcomopleto_1_s[0]),
    .B(demultiplexer_2_out1[1]), .A(demultiplexer_2_out1[0]));
  Multiplexer #(.width(2), .enable("false")) multiplexer_1 (
    .in0(meiosomador_1_s), .in1(meiosubtrator_1_s), .out(out_7), .sel(in_3));
  Multiplexer #(.width(2), .enable("false")) multiplexer_2 (
    .in0(somadorcompleto_1_s), .in1(subtratorcomopleto_1_s), .out(out_8), .sel(in_6));

  // Notes on the sheet:
  //   Meio Somador
  //   Meio Subtrator
  //   Somador Completo
  //   Subtrator Completo
endmodule

module meioSomador (
  input  A,
  input  B,
  output S,
  output Cout
);

  xor xor_1 (S, A, B);
  and and_1 (Cout, A, B);
endmodule

module somadorCompleto (
  input  A,
  input  B,
  input  Cin,
  output S,
  output Cout
);

  wire meiosomador_1_cout, meiosomador_1_s, meiosomador_2_cout;

  meioSomador meiosomador_1 (.Cout(meiosomador_1_cout), .S(meiosomador_1_s), .A(A), .B(B));
  meioSomador meiosomador_2 (.Cout(meiosomador_2_cout), .S(S), .A(meiosomador_1_s), .B(Cin));
  or or_1 (Cout, meiosomador_2_cout, meiosomador_1_cout);
endmodule

module somador_4bits (
  input  [3:0] A,
  input  [3:0] B,
  output [3:0] S
);

  wire somadorcompleto_1_cout, somadorcompleto_2_cout, somadorcompleto_3_cout, somadorcompleto_4_cout;

  somadorCompleto somadorcompleto_1 (
    .B(B[3]), .Cout(somadorcompleto_1_cout), .Cin(somadorcompleto_2_cout), .S(S[3]), .A(A[3]));
  somadorCompleto somadorcompleto_2 (
    .B(B[2]), .Cout(somadorcompleto_2_cout), .Cin(somadorcompleto_3_cout), .S(S[2]), .A(A[2]));
  Hex_Digit_Display hex_digit_display_1 (.value(S));  // open: dp
  somadorCompleto somadorcompleto_3 (
    .B(B[1]), .Cout(somadorcompleto_3_cout), .Cin(somadorcompleto_4_cout), .S(S[1]), .A(A[1]));
  somadorCompleto somadorcompleto_4 (.B(B[0]), .Cout(somadorcompleto_4_cout), .Cin(1'b0), .S(S[0]), .A(A[0]));
  // also tied to GND on the sheet: somadorcompleto_1_cout
endmodule

module meioSubtrator (
  input  A,
  input  B,
  output S,
  output Tout
);

  wire not_1_out;

  xor xor_1 (S, A, B);
  and and_1 (Tout, A, not_1_out);
  not not_1 (not_1_out, B);
endmodule

module subtratorComopleto (
  input  A,
  input  B,
  input  Bin,
  output S,
  output Bout
);

  wire meiosubtrator_1_s, meiosubtrator_1_tout, meiosubtrator_2_tout;

  meioSubtrator meiosubtrator_1 (.S(meiosubtrator_1_s), .Tout(meiosubtrator_1_tout), .B(B), .A(A));
  meioSubtrator meiosubtrator_2 (.S(S), .Tout(meiosubtrator_2_tout), .B(Bin), .A(meiosubtrator_1_s));
  or or_1 (Bout, meiosubtrator_2_tout, meiosubtrator_1_tout);
endmodule

module complementoDois (
  input  [3:0] A,
  input  [3:0] B,
  input  Cin,
  output Cout,
  output [3:0] S
);

  wire multiplexer_1_out, multiplexer_3_out, multiplexer_4_out, not_1_out, not_2_out, not_4_out,
       somadorcompleto_2_cout, somadorcompleto_3_cout, somadorcompleto_4_cout;

  not not_1 (not_1_out, B[3]);
  Multiplexer #(.enable("false")) multiplexer_1 (.in0(B[3]), .in1(not_1_out), .out(multiplexer_1_out), .sel(Cin));
  somadorCompleto somadorcompleto_1 (
    .B(multiplexer_1_out), .Cout(Cout), .Cin(somadorcompleto_2_cout), .S(S[3]), .A(A[3]));
  not not_2 (not_2_out, B[2]);
  Multiplexer #(.enable("false")) multiplexer_2 (.in0(B[2]), .in1(not_2_out), .sel(Cin));  // open: out
  somadorCompleto somadorcompleto_2 (
    .Cout(somadorcompleto_2_cout), .Cin(somadorcompleto_3_cout), .S(S[1]), .A(A[2]));  // open: B
  // NOT_Gate not_3 has open pins: in=B[1], out=open
  Multiplexer #(.enable("false")) multiplexer_3 (.in0(B[1]), .out(multiplexer_3_out), .sel(Cin));  // open: in1
  somadorCompleto somadorcompleto_3 (
    .B(multiplexer_3_out), .Cout(somadorcompleto_3_cout), .Cin(somadorcompleto_4_cout), .S(S[2]), .A(A[1]));
  not not_4 (not_4_out, B[0]);
  Multiplexer #(.enable("false")) multiplexer_4 (.in0(B[0]), .in1(not_4_out), .out(multiplexer_4_out), .sel(Cin));
  somadorCompleto somadorcompleto_4 (
    .B(multiplexer_4_out), .Cout(somadorcompleto_4_cout), .Cin(Cin), .S(S[0]), .A(A[0]));
endmodule

module Multiplicador (
  input  A0,
  input  A1,
  input  B1,
  input  B0,
  output P3,
  output P2,
  output P1,
  output P0
);

  wire and_1_out, and_2_out, and_3_out, and_4_out, meiosomador_2_cout;

  and and_1 (and_1_out, A1, B1);
  meioSomador meiosomador_1 (.Cout(P3), .S(P2), .A(meiosomador_2_cout), .B(and_1_out));
  and and_2 (and_2_out, A1, B0);
  and and_3 (and_3_out, A0, B1);
  meioSomador meiosomador_2 (.Cout(meiosomador_2_cout), .S(P1), .A(and_3_out), .B(and_2_out));
  and and_4 (and_4_out, A0, B0);
endmodule

module registradorParalelo (
  input  [3:0] D,
  input  Clock,
  input  Carga,
  input  Clear,
  output [3:0] Q
);

  wire multiplexer_1_out, multiplexer_2_out, multiplexer_3_out, multiplexer_4_out;

  Multiplexer #(.enable("false")) multiplexer_1 (.in0(Q[3]), .in1(D[3]), .out(multiplexer_1_out), .sel(Carga));
  D_Flip_Flop d_ff_1 (.D(multiplexer_1_out), .clk(Clock), .Q(Q[3]), .reset(Clear));  // open: Qn, preset
  Multiplexer #(.enable("false")) multiplexer_2 (.in0(Q[2]), .in1(D[2]), .out(multiplexer_2_out), .sel(Carga));
  D_Flip_Flop d_ff_2 (.D(multiplexer_2_out), .clk(Clock), .Q(Q[2]), .reset(Clear));  // open: Qn, preset
  D_Flip_Flop d_ff_3 (.D(multiplexer_3_out), .clk(Clock), .Q(Q[1]), .reset(Clear));  // open: Qn, preset
  Multiplexer #(.enable("false")) multiplexer_3 (.in0(Q[1]), .in1(D[1]), .out(multiplexer_3_out), .sel(Carga));
  Multiplexer #(.enable("false")) multiplexer_4 (.in0(Q[0]), .in1(D[0]), .out(multiplexer_4_out), .sel(Carga));
  D_Flip_Flop d_ff_4 (.D(multiplexer_4_out), .clk(Clock), .Q(Q[0]), .reset(Clear));  // open: Qn, preset
endmodule
