// Logisim project Projeto2.circ as structural Verilog: 1 circuit, main circuit main
module main (
);

  wire ALU_SRC, and_1_out, and_2_out, and_3_out, and_5_out, CLK, LOAD, MEM_TO_REG, REG_DEST, REG_W,
       registerfile_1_p7, STORE;
  wire [3:1] ALU_OP;
  wire [4:0] multiplexer_1_out;
  wire [5:0] FUNCT;
  wire [11:0] mips_alu_1_p4_2;
  wire [19:0] mips_alu_1_p4;
  wire [31:0] adder_1_out, bit_extender_1_out, mips_ram_1_p2, mips_ram_1_p6, multiplexer_2_out, register_1_q,
       registerfile_1_p1;
  wire [31:6] mipsprogramrom_1_p2;

  Clock clock_1 (.out(CLK));
  Adder #(.width(32)) adder_1 (.a(register_1_q), .b(32'h4), .out(adder_1_out));  // open: cin, cout
  Register #(.width(32)) register_1 (.D(adder_1_out), .Q(register_1_q), .clk(CLK));  // open: en, clr
  // MIPSProgramROM mipsprogramrom_1: pin names not known; wires that end beside it: register_1_q, {mipsprogramrom_1_p2, FUNCT}
  Multiplexer #(.width(5)) multiplexer_1 (
    .in0(mipsprogramrom_1_p2[15:11]), .in1(mipsprogramrom_1_p2[20:16]), .out(multiplexer_1_out),
    .sel(REG_DEST));  // open: en
  and and_1 (and_1_out, mipsprogramrom_1_p2[26], ~mipsprogramrom_1_p2[27], ~mipsprogramrom_1_p2[28], mipsprogramrom_1_p2[29], ~mipsprogramrom_1_p2[30], ~mipsprogramrom_1_p2[31]);  // AND_Gate
  and and_2 (and_2_out, mipsprogramrom_1_p2[26], mipsprogramrom_1_p2[27], ~mipsprogramrom_1_p2[28], mipsprogramrom_1_p2[29], ~mipsprogramrom_1_p2[30], mipsprogramrom_1_p2[31]);  // AND_Gate
  and and_3 (and_3_out, mipsprogramrom_1_p2[26], mipsprogramrom_1_p2[27], ~mipsprogramrom_1_p2[28], ~mipsprogramrom_1_p2[29], ~mipsprogramrom_1_p2[30], mipsprogramrom_1_p2[31]);  // AND_Gate
  and and_4 (ALU_OP[3], FUNCT[0], FUNCT[1], FUNCT[2], ~FUNCT[3], ~FUNCT[4], FUNCT[5]);  // AND_Gate
  and and_5 (and_5_out, FUNCT[0], ~FUNCT[1], ~FUNCT[2], ~FUNCT[3], ~FUNCT[4], FUNCT[5]);  // AND_Gate
  assign bit_extender_1_out = {{16{1'b0}}, {mipsprogramrom_1_p2[15:6], FUNCT}};  // Bit_Extender bit_extender_1
  // RegisterFile registerfile_1: pin names not known; wires that end beside it: registerfile_1_p1, CLK, REG_W, multiplexer_1_out, mipsprogramrom_1_p2[25:21], mipsprogramrom_1_p2[20:16], registerfile_1_p7
  Multiplexer #(.width(32)) multiplexer_2 (
    .in0(mips_ram_1_p2), .in1(bit_extender_1_out), .out(multiplexer_2_out), .sel(ALU_SRC));  // open: en
  // Mips_ALU mips_alu_1: pin names not known; wires that end beside it: registerfile_1_p7, multiplexer_2_out, {{2{ALU_OP[3]}}, ALU_OP[1], 1'b0}, {mips_alu_1_p4_2, mips_alu_1_p4}
  or or_1 (ALU_OP[1], and_1_out, and_5_out, ALU_OP[3]);
  or or_2 (REG_DEST, and_1_out, and_2_out, and_3_out);
  or or_3 (ALU_SRC, and_1_out, and_2_out, and_3_out);
  or or_4 (REG_W, and_1_out, and_2_out, and_5_out, and_3_out, ALU_OP[3]);
  and and_6 (STORE, and_2_out, ~and_3_out);  // AND_Gate
  and and_7 (LOAD, ~and_2_out, and_3_out);  // AND_Gate
  and and_8 (MEM_TO_REG, ~and_1_out, ~and_2_out, and_3_out);  // AND_Gate
  Multiplexer #(.width(32)) multiplexer_3 (
    .in0({mips_alu_1_p4_2, mips_alu_1_p4}), .in1(mips_ram_1_p6), .out(registerfile_1_p1), .sel(MEM_TO_REG));  // open: en
  // MIPS_RAM mips_ram_1: pin names not known; wires that end beside it: mips_alu_1_p4, mips_ram_1_p2, STORE, CLK, LOAD, mips_ram_1_p6

  // Other names for the same wires on the sheet: ALU_OP[2] = ALU_OP[3]

  // Notes on the sheet:
  //   OP
  //   Funct
  //   S.A.
  //   R
  //   I
  //   End. a ser Gravado
  //   Imediato do Tipo I
  //   End. do Registrador Lido por A
  //   Dado a ser Guardado
  //   End do Registrador Lido por B
  //   NOR
  //   ADDU
  //   Converte o Imediato pra 32 Bits
  //   ADDIU
  //   STORE
  //   LOAD
  //   End Base
  //   Offset (imediato)
  //   R
  //   I
  //   Operacao a ser Realizada
  //   Dado Recebido
  //   liga so no load
endmodule
