// Logisim project circuito1.circ as structural Verilog: 1 circuit, main circuit main
module main (
  input  [3:0] in_1,
  input  Habilita_Gravacao
);

  wire clock_1_out, clock_2_out, registerfile_1_p1, registerfile_1_p7, registerfile_1_p8;
  wire [31:0] adder_1_out, mipsprogramrom_1_p2, register_1_q;

  Adder #(.width(32)) adder_1 (.a(register_1_q), .b(32'h4), .out(adder_1_out));  // open: cin, cout
  Register #(.width(32)) register_1 (.D(adder_1_out), .Q(register_1_q), .clk(clock_1_out));  // open: en, clr
  Clock clock_1 (.out(clock_1_out));
  // MIPSProgramROM mipsprogramrom_1: pin names not known; wires that end beside it: register_1_q, mipsprogramrom_1_p2
  Clock clock_2 (.out(clock_2_out));
  // RegisterFile registerfile_1: pin names not known; wires that end beside it: registerfile_1_p1, clock_2_out, Habilita_Gravacao, mipsprogramrom_1_p2[15:11], mipsprogramrom_1_p2[25:21], mipsprogramrom_1_p2[20:16], registerfile_1_p7, registerfile_1_p8
  // Mips_ALU mips_alu_1: pin names not known; wires that end beside it: registerfile_1_p7, registerfile_1_p8, in_1, registerfile_1_p1

  // Notes on the sheet:
  //   Funct
  //   SA
  //   Destino
  //   Segunda Origem
  //   Primeira Origem
  //   OP
  //   Ccodigo de Maquina
  //   End. a ser Gravado
  //   Clock
  //   End. do Registrador Lido por A
  //   End do Registrador Lido por B
  //   Dado a ser Guardado
  //   Operacao a ser Realizada
endmodule
