// Logisim project circuito2.circ as structural Verilog: 1 circuit, main circuit main
module main (
  input  MEM_TO_REG,
  input  in_2,
  input  [3:0] in_3,
  input  STORE,
  input  Habilita_Gravacao,
  input  I
);

  wire clock_1_out, clock_2_out, registerfile_1_p7;
  wire [4:0] multiplexer_1_out;
  wire [31:0] adder_1_out, bit_extender_1_out, mips_alu_1_p2, mips_alu_1_p4, mips_ram_1_p4,
       mipsprogramrom_1_p2, register_1_q, registerfile_1_p1, registerfile_1_p8;

  Adder #(.width(32)) adder_1 (.a(register_1_q), .b(32'h4), .out(adder_1_out));  // open: cin, cout
  Register #(.width(32)) register_1 (.D(adder_1_out), .Q(register_1_q), .clk(clock_1_out));  // open: en, clr
  Clock clock_1 (.out(clock_1_out));
  // MIPSProgramROM mipsprogramrom_1: pin names not known; wires that end beside it: register_1_q, mipsprogramrom_1_p2
  Multiplexer #(.width(5)) multiplexer_1 (
    .in0(mipsprogramrom_1_p2[15:11]), .in1(mipsprogramrom_1_p2[20:16]), .out(multiplexer_1_out), .sel(in_2));  // open: en
  Clock clock_2 (.out(clock_2_out));
  assign bit_extender_1_out = {{16{1'b0}}, mipsprogramrom_1_p2[15:0]};  // Bit_Extender bit_extender_1
  // RegisterFile registerfile_1: pin names not known; wires that end beside it: registerfile_1_p1, clock_2_out, Habilita_Gravacao, multiplexer_1_out, mipsprogramrom_1_p2[25:21], mipsprogramrom_1_p2[20:16], registerfile_1_p7, registerfile_1_p8
  // Mips_ALU mips_alu_1: pin names not known; wires that end beside it: registerfile_1_p7, mips_alu_1_p2, in_3, mips_alu_1_p4
  Multiplexer #(.width(32)) multiplexer_2 (
    .in0(registerfile_1_p8), .in1(bit_extender_1_out), .out(mips_alu_1_p2), .sel(I));  // open: en
  Multiplexer #(.width(32)) multiplexer_3 (
    .in0(mips_alu_1_p4), .in1(mips_ram_1_p4), .out(registerfile_1_p1), .sel(MEM_TO_REG));  // open: en
  // MIPS_RAM mips_ram_1: pin names not known; wires that end beside it: mips_alu_1_p4[19:0], registerfile_1_p8, STORE, mips_ram_1_p4, mips_ram_1_p4

  // Notes on the sheet:
  //   R ou I (REG_DEST)
  //   Funct
  //   S.A.
  //   R
  //   I
  //   End. a ser Gravado
  //   Imediato do Tipo I
  //   Clock
  //   End. do Registrador Lido por A
  //   End do Registrador Lido por B
  //   Dado a ser Guardado
  //   Converte o Imediato pra 32 Bits
  //   End Base
  //   Offset (imediato)
  //   R
  //   ALU_SRC
  //   Operacao a ser Realizada
  //   Dado Recebido
  //   liga so no load
endmodule
